# Fritzing sketch Nani (saved by Fritzing 0.9.6b)
circuit board: 8.46667cm x 5.64444cm
breadboards: 1

parts:
  Q1 = NPN-Transistor [package="SOT-23 [SMD]"]
  R1 = Resistor [tolerance=±5% resistance=100k package="2010 [SMD]"]
  R2 = Resistor [tolerance=±5% resistance=100k package="2010 [SMD]"]
  R3 = Resistor [tolerance=±5% resistance=10k package="2010 [SMD]"]
  R4 = Resistor [tolerance=±5% resistance=10k package="2010 [SMD]"]
  D1 = Diode [package=diode-1n4148]
  C1 = Ceramic Capacitor [capacitance=1µF voltage=20V package="0805 [SMD, multilayer]"]
  U1 = RELAY [package=relay-t9a-2]
  Q3 = PNP-Transistor [package="SOT-23 [SMD]"]
  V1 = DC Power [voltage=5]

nets:
  N1: Q1.2, D1.A, U1.COIL2
  N2: Q1.0, R1.Pin_1, R3.Pin_0
  N3: Q1.1, R2.Pin_0, C1.0
  N4: R2.Pin_1, R4.Pin_0, Q3.0
  N5: R3.Pin_1, D1.C, U1.COIL1, Q3.1
  N6: R4.Pin_1, C1.1, Q3.2, V1.V-
