# Fritzing sketch flashing led circuit (saved by Fritzing 0.9.6b)
circuit board: 8.46667cm x 5.64444cm
breadboards: 1

parts:
  U1 = 555 Timer [package="SO8 [SMD]"]
  LED1 = LED - 5mm [color="Red (633nm)" current=0.030 package="5 mm [THT]"]
  R1 = Resistor [tolerance=±5% power=0.25 resistance=1k package=THT]
  R2 = Resistor [tolerance=±5% power=0.25 resistance=470 package=THT]
  R3 = Resistor [tolerance=±5% power=0.25 resistance=1k package=THT]
  C1 = Ceramic Capacitor [capacitance=1µF voltage=35V package="200 mil [THT, multilayer]"]
  V1 = DC Power [voltage=5]

nets:
  N1: U1.Pin_1, LED1.cathode, C1.0, V1.V-
  N2: U1.Pin_2, U1.Pin_6, R2.Pin_0, C1.1
  N3: U1.Pin_3, R3.Pin_1
  N4: U1.Pin_4, U1.Pin_8, R1.Pin_1, V1.V+
  N5: U1.Pin_7, R1.Pin_0, R2.Pin_1
  N6: LED1.anode, R3.Pin_0
